# Fritzing sketch midboard sketch 031319a (saved by Fritzing 0.9.3b)

parts:
  Part2 = Adafruit Thermocouple Amplifier MAX31855 [part_number="Adafruit #269"]
  Part3 = Adafruit Perma-Proto HAT [part_number="Adafruit #2314 and #2310"]
  R1 = Resistor [tolerance=±5% resistance=220 package="0805 [SMD]"]
  LED1 = LED - 5mm [color="Red (633nm)" package="5 mm [THT]"]

nets:
  N1: Part2.VIN, Part3.N$44#289
  N2: Part2.+3V3, Part3.N$45
  N3: Part2.GND, Part3.N$46#299
  N4: Part2.DO, Part3.N$47#304
  N5: Part2.CS, Part3.N$48#309
  N6: Part2.CLK, Part3.N$50#319
  N7: Part3.SCL, Part3.GPIO17
  N8: Part3.SPI_CE1, Part3.N$50#316
  N9: Part3.GPIO5, Part3.N$48#306
  N10: Part3.GPIO16, Part3.N$47#301
  N11: Part3.GPIO21, Part3.N$39#267
  N12: Part3.3.3V, Part3.N$44#286
  N13: Part3.GND, Part3.N$22#260, Part3.N$46#296
  N14: Part3.N$22#256, LED1.cathode
  N15: Part3.N$23#261, LED1.anode
  N16: Part3.N$23#264, R1.Pin_1
  N17: Part3.N$39#269, R1.Pin_0

custom parts:
  Adafruit Thermocouple Amplifier MAX31855: Thermocouples are very sensitive, requiring a good amplifier with a cold-compensation reference. The MAX31855K does everything for you, and can be easily interfaced with any microcontroller, even one without an analog input. This breakout board has the chip itself, a 3.3V regulator with 10uF bypass capacitors and level shifting circuitry, all assembled and tested. Comes with a 2 pin terminal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
  Adafruit Perma-Proto HAT: To kick off the Adafruit HAT party, we have this Perma-Proto inspired plug in daughter board. It has a grid of 0.1" prototyping soldering holes for attaching chips, resistors, LED, potentiometers and more. The holes are connected underneath with traces to mimic the solderless breadboards you're familiar. There's also long power strips for +3V, +5V and Ground connections to the Pi. Near the top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
